# Fritzing sketch pico_motor_controller (saved by Fritzing 0.9.9b)
breadboards: 1

parts:
  Mod1 = Raspberry Pi Pico
  R1 = Resistor [tolerance=±5% power=0.25 resistance=220 package=THT]
  S1 = Toggle Switch [package=THT]
  S2 = Toggle Switch [package=THT]
  LED2 = LED - 5mm [color="Red (633nm)" current=0.030 package="5 mm [THT]"]
  LED3 = LED - 5mm [color="Blue (470nm)" current=0.030 package="5 mm [THT]"]
  J1 = female pin header, 2 pins [form="♀ (female)"]
  J2 = female pin header, 2 pins [form="♀ (female)"]
  J3 = female pin header, 2 pins [form="♀ (female)"]
  J4 = female pin header, 2 pins [form="♀ (female)"]
  Pololu_A1 = Pololu A4988 [package=SO16]
  J5 = female pin header, 2 pins [form="♀ (female)"]
  J6 = female pin header, 2 pins [form="♀ (female)"]
  LED1 = LED - 3mm [color="Green (570nm)" current=0.030 package="3 mm [THT]"]
  R2 = Resistor [tolerance=±5% power=0.25 resistance=220 package=THT]
  R3 = Resistor [tolerance=±5% power=0.25 resistance=220 package=THT]

nets:
  N1: Mod1.pin_3, Mod1.pin_8, Mod1.pin_13, Mod1.pin_18, Mod1.pin_23, Mod1.pin_28, Mod1.pin_33, Mod1.pin_38, Mod1.pin_42, S1.L2, S2.L2, LED2.cathode, J1.pin1, J1.pin2, J2.pin1, J2.pin2, LED1.cathode
  N2: Mod1.pin_14, Pololu_A1.VDD, J5.pin1
  N3: Mod1.pin_15, Pololu_A1.1A, J5.pin2
  N4: Mod1.pin_16, LED3.cathode, Pololu_A1.GND, J6.pin1, R2.Pin_0
  N5: Mod1.pin_17, R1.Pin_0, Pololu_A1.1B, J6.pin2
  N6: Mod1.pin_24, S1.L1, J3.pin2
  N7: Mod1.pin_25, S2.L1, J3.pin1
  N8: Mod1.pin_26, J4.pin2
  N9: Mod1.pin_27, J4.pin1
  N10: Mod1.pin_36, R3.Pin_1
  N11: R1.Pin_1, LED1.anode
  N12: LED2.anode, R2.Pin_1
  N13: LED3.anode, R3.Pin_0

custom parts:
  Raspberry Pi Pico: Raspberry Pi Pico. Based around the RP2040 microcontroller the Pico is a low cost microcontroller device bringing Raspberry Pi quality, cost, and easy of use to the microcontroller space. Jan 2021, Split part in to two versions: tht (this one) and SMD. This one will drill holes for a .1 in header in pcb to allow plugging in the module as well as providing pads to solder the module to the top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
